# Fritzing sketch esptherm-batt-cap (saved by Fritzing 0.9.2b)
perfboards: 1

parts:
  R4 = Resistor [tolerance=±5% resistance=4.7k package=THT]
  JP8 = Header 3 [package=screwterminal-3.5mm-3_lock.007s]
  S2 = Pushbutton [package="[SMD]"]
  DS5 = DS18B20 1-Wire Temperature Sensor [part_number=DS18B20]
  C1 = Electrolytic Capacitor [capacitance=10µF package="100 mil [THT, electrolytic]"]
  C7 = Electrolytic Capacitor [capacitance=0.47mF package="300 mil [THT, electrolytic]"]

nets:
  N1: R4.Pin_0, DS5.DQ
  N2: R4.Pin_1, DS5.GND, C1.+, C7.+
  N3: JP8.1, S2.Pin_3, S2.Pin_4, DS5.VDD, C1.-, C7.-
  N4: S2.Pin_1, S2.Pin_2

notes:
  GPIO0
  TTL-RX
  TTL-TX
  GND
