# Fritzing sketch esptherm-batt (saved by Fritzing 0.9.2b)
perfboards: 1

parts:
  R4 = Resistor [tolerance=±5% resistance=4.7k package=THT]
  DS4 = DS18B20 1-Wire Temperature Sensor [part_number=DS18B20]
  JP8 = Header 3 [package=screwterminal-3.5mm-3_lock.007s]
  S2 = Pushbutton [package="[SMD]"]
  VCC2 = Battery

nets:
  N1: R4.Pin_0, DS4.DQ
  N2: R4.Pin_1, DS4.GND, VCC2.+
  N3: DS4.VDD, JP8.1, S2.Pin_3, S2.Pin_4, VCC2.-
  N4: S2.Pin_1, S2.Pin_2

notes:
  GPIO0
  TTL-RX
  TTL-TX
  GND
